# Fritzing sketch SmartCar (saved by Fritzing 0.7.4b)
breadboards: 1

parts:
  Arduino1 = Arduino  # not connected
  Composants1 = Arduino Musical Instrument Shield
  Composants2 = DeuLigne 1.1 - The Snootlab's LCD shield for Arduino  # not connected
  J1 = Piezo Speaker

nets:
  N1: Composants1.GBUF, J1.pin1
  N2: Composants1.LEFT, J1.pin2
